# Fritzing sketch TrainRemoteDiagram (saved by Fritzing 0.9.3b)
breadboards: 1
perfboards: 1

parts:
  IC1 = IC, DIP package, 8 pins [chip_label=IC]
  S1 = Pushbutton [package="[THT]"]
  S2 = Pushbutton [package="[THT]"]
  R1 = Resistor [tolerance=±5% resistance=2.2k package=THT]  # not connected
  Part1 = Arduino Uno (Rev3)
  R2 = Resistor [tolerance=±5% resistance=2.2k package=THT]
  R3 = Resistor [tolerance=±5% resistance=2.2k package=THT]
  U1 = POT [package=pot_alpha_rv16af-20]
  S4 = Toggle Switch [package=THT]
  LED1 = LED - 5mm [color="Red (633nm)" package="5 mm [THT]"]  # not connected
  S5 = Toggle Switch [package=THT]  # not connected
  S3 = Pushbutton [package="[THT]"]

nets:
  N1: IC1.pin1, U1.A
  N2: IC1.pin2, S4.L2
  N3: IC1.pin3, U1.E
  N4: IC1.pin4, Part1.GND
  N5: IC1.pin5, Part1.D13/SCK
  N6: IC1.pin6, Part1.D4
  N7: IC1.pin7, Part1.D3_PWM
  N8: IC1.pin8, Part1.3V3
  N9: S1.Pin_1, S1.Pin_2, S1.Pin_3, S1.Pin_4
  N10: S2.Pin_1, S2.Pin_2, S2.Pin_3, S2.Pin_4, R3.Pin_1
  N11: Part1.D10_PWM/SS, R3.Pin_0
  N12: Part1.D11_PWM/MOSI, R2.Pin_0
  N13: R2.Pin_1, S3.Pin_1, S3.Pin_2, S3.Pin_3, S3.Pin_4
  N14: U1.S, S4.L1
